# Fritzing sketch DC - DC Elevador (saved by Fritzing 0.9.0b)
breadboards: 1

parts:
  Opto1 = Optocoupler [package=THT]
  R1 = Resistor [tolerance=±5% resistance=220 package=THT]
  J1 = female pin header, 4 pins [form="♀ (female)"]
  Batt = Screw terminal - 2 pins [package=THT]
  U1 = 555 Timer [package="DIP8 [THT]"]
  C1 = Electrolytic Capacitor [capacitance=10µF voltage=16V package="100 mil [THT, electrolytic]"]
  C2 = Electrolytic Capacitor [capacitance=100µF voltage=16V package="100 mil [THT, electrolytic]"]
  R3 = Resistor [tolerance=±5% resistance=10k package=THT]
  C3 = Ceramic Capacitor [capacitance=3.3nF voltage=35V package="100 mil [THT, multilayer]"]
  ZVP2106A = MOSFET-NCHANNEL [package=to-92]
  R5 = Resistor [tolerance=±5% resistance=2k package=THT]
  L1 = Inductor [package="400 mil [THT]"]
  L2 = Inductor [package="400 mil [THT]"]
  C5 = Ceramic Capacitor [capacitance=2.2µF voltage=250V package="200 mil [THT, multilayer]"]
  IRF450 = mystery part, 3 pins [chip_label=?]
  R6 = Resistor [tolerance=±5% resistance=10M package=THT]
  R7 = Resistor [tolerance=±5% resistance=200k package=THT]
  R4 = Resistor [tolerance=±5% resistance=20k package=THT]
  R8 = Resistor [tolerance=±5% resistance=100k package=THT]
  BYW95C = Screw terminal - 2 pins [package=THT]
  D1 = Rectifier Diode [part_number=1N4001 package="300 mil [THT]"]
  J2 = screw terminal, 3 pins  # not connected
  Opto2 = Optocoupler [package=THT]
  J3 = Screw terminal - 2 pins [package=THT]
  R9 = Resistor [tolerance=±5% resistance=220 package=THT]
  R10 = Resistor [tolerance=±5% resistance=100k package=THT]

nets:
  N1: Opto1.Pin_1, R1.Pin_0
  GND_1: Opto1.Pin_2, Opto1.Pin_3, J1.pin3, Opto2.Pin_2
  S_IN: Opto1.Pin_5, U1.Reset, R8.Pin_1
  N2: R1.Pin_1, J1.pin4
  Disparo: J1.pin2, R9.Pin_1
  GND: Batt.pin1, U1.Ground, C1.-, C2.-, C3.0, ZVP2106A.S, C5.0, IRF450.pin1, R7.Pin_1, Opto2.Pin_4
  12V/Vbatt: Batt.pin2, U1.Vcc_Supply_Voltage, C1.+, C2.+, R5.Pin_0, L2.pin_1, R4.Pin_0, R8.Pin_0, R10.Pin_0
  N3: U1.Trigger, U1.Threshold, R3.Pin_1, C3.1
  N4: U1.Output, IRF450.pin3
  N5: U1.Control_Voltage, ZVP2106A.D, R5.Pin_1
  N6: U1.Discharge, R3.Pin_0, R4.Pin_1
  Vref: ZVP2106A.G, R6.Pin_1, R7.Pin_0
  N7: L1.pin_0, IRF450.pin2, BYW95C.Anodo
  N8: L1.pin_1, L2.pin_0
  N9: C5.1, BYW95C.Catodo, D1.cathode, J3.pin1
  N10: D1.anode, J3.pin2
  N11: Opto2.Pin_1, R9.Pin_0
  N12: Opto2.Pin_5, R10.Pin_1

notes:
  DC - DC Elevador, Disparador Futbot 1.0v
  Futbot USB

custom parts:
  Screw terminal - 2 pins: Screw terminal with 2 pins
